# Fritzing sketch solarem1 (saved by Fritzing 0.9.3b)
breadboards: 1

parts:
  Raspberry_Pi_1 = Raspberry Pi 3 [part_number=RPI-3-V1.2]
  J1 = Camdenboss CTB0158-10 [part_number=8-Relettä package=THT]
  J2 = Camdenboss CTB0158-3 [part_number=8-relettä package=THT]

nets:
  GND: Raspberry_Pi_1.GND, J1.GND, J2.GND
  N1: Raspberry_Pi_1.GPIO17, J1.IN1
  N2: Raspberry_Pi_1.GPIO27, J1.IN3
  N3: Raspberry_Pi_1.GPIO22, J1.IN4
  N4: Raspberry_Pi_1.GPIO5, J1.IN8
  N5: Raspberry_Pi_1.GPIO25, J1.IN7
  N6: Raspberry_Pi_1.GPIO24, J1.IN6
  N7: Raspberry_Pi_1.GPIO23, J1.IN5
  N8: Raspberry_Pi_1.GPIO18, J1.IN2
  5V: Raspberry_Pi_1.5V, J1.VCC
  N9: J2.VCC, J2.J0-VCC

custom parts:
  Camdenboss CTB0158-10: Camdenboss CTB0158-10 5.08mm (0.2") Pitch Standard Profile 90 ̊ Rising Clamp Terminal, 10 pole The real-life connectors are modular, made up of two or three connector blocks slotted together. These can be further slotted together to make larger connectors. Fritzing part is derived from Screw terminals by Lionel Michel. Because of the offset between connection pins and screw terminals, these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
  Camdenboss CTB0158-3: Camdenboss CTB0158-3 5.08mm (0.2") Pitch Standard Profile 90 ̊ Rising Clamp Terminal, 3 pole The real-life connectors are modular, made up of two or three connector blocks slotted together. These can be further slotted together to make larger connectors. Fritzing part is derived from Screw terminals by Lionel Michel. Because of the offset between connection pins and screw terminals, these are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
